# Fritzing sketch Schematic (saved by Fritzing 0.9.9b)
breadboards: 2

parts:
  MH-ET_LIVE_ESP32_DEVKIT1 = MH-ET LIVE ESP32 DEVKIT 38 pins
  Pressure_Sensor = Rotary Potentiometer (Small) [maximum_resistance=100kΩ package=THT]

nets:
  N1: MH-ET_LIVE_ESP32_DEVKIT1.3V3, Pressure_Sensor.leg1
  N2: MH-ET_LIVE_ESP32_DEVKIT1.IO27, Pressure_Sensor.wiper
  N3: MH-ET_LIVE_ESP32_DEVKIT1.GND#70, Pressure_Sensor.leg2

custom parts:
  MH-ET LIVE ESP32 DEVKIT 38 pins: http://mh.nodebb.com/topic/2/mh-et-live-esp32-devkit
